// Logisim project SPM.circ as structural Verilog: 9 circuits, main circuit TCMP
module TCMP (
  input  A,
  input  clk,
  input  reset,
  output out_4
);

  wire d_ff_2_q, FDHA_out, or_1_out, xor_1_out;

  and FDHA (FDHA_out, A, d_ff_2_q);
  xor xor_1 (xor_1_out, A, d_ff_2_q);
  D_Flip_Flop #(.trigger("high")) d_ff_1 (.clk(clk), .D(xor_1_out), .Q(out_4), .reset(reset));  // open: Qn, preset, en
  or or_1 (or_1_out, A, d_ff_2_q);
  D_Flip_Flop #(.trigger("high")) d_ff_2 (
    .clk(clk), .D(or_1_out), .Q(d_ff_2_q), .reset(reset));  // open: Qn, preset, en
endmodule

module unit_digit (
  input  p3,
  input  p2,
  input  p1,
  input  p0,
  output a,
  output b,
  output c,
  output d,
  output e,
  output f,
  output g
);

  wire and_1_out, and_2_out, and_3_out, and_4_out, and_5_out, and_6_out, and_7_out, and_8_out, and_9_out,
       and_10_out, and_11_out, and_12_out, and_13_out, and_14_out, and_15_out, and_16_out, not_1_out,
       not_2_out, not_3_out, not_4_out, not_5_out, not_6_out, not_7_out, not_8_out, not_9_out, not_10_out,
       not_11_out, not_12_out, not_13_out, not_14_out, not_15_out, not_16_out, not_17_out, not_18_out,
       not_19_out, not_20_out, not_21_out;

  not not_1 (not_1_out, p2);
  and and_1 (and_1_out, not_1_out, not_2_out);
  not not_2 (not_2_out, p0);
  and and_2 (and_2_out, p2, p0);
  not not_3 (not_3_out, p2);
  not not_4 (not_4_out, p1);
  and and_3 (and_3_out, not_4_out, not_5_out);
  not not_5 (not_5_out, p0);
  and and_4 (and_4_out, p1, p0);
  not not_6 (not_6_out, p1);
  or or_1 (c, not_6_out, p0, p2);
  not not_7 (not_7_out, p2);
  and and_5 (and_5_out, not_7_out, not_8_out);
  not not_8 (not_8_out, p0);
  not not_9 (not_9_out, p2);
  and and_6 (and_6_out, not_9_out, p1);
  and and_7 (and_7_out, p1, not_10_out);
  not not_10 (not_10_out, p0);
  not not_11 (not_11_out, p1);
  and and_8 (and_8_out, p2, not_11_out, p0);
  not not_12 (not_12_out, p2);
  and and_9 (and_9_out, not_12_out, not_13_out);
  not not_13 (not_13_out, p0);
  and and_10 (and_10_out, p1, not_14_out);
  not not_14 (not_14_out, p0);
  not not_15 (not_15_out, p1);
  and and_11 (and_11_out, not_15_out, not_16_out);
  not not_16 (not_16_out, p0);
  and and_12 (and_12_out, p2, not_17_out);
  not not_17 (not_17_out, p1);
  and and_13 (and_13_out, p2, not_18_out);
  not not_18 (not_18_out, p0);
  not not_19 (not_19_out, p2);
  and and_14 (and_14_out, not_19_out, p1);
  and and_15 (and_15_out, p2, not_20_out);
  not not_20 (not_20_out, p1);
  and and_16 (and_16_out, p2, not_21_out);
  not not_21 (not_21_out, p0);
  or or_2 (a, and_1_out, p1, and_2_out, p3);
  or or_3 (b, not_3_out, and_3_out, and_4_out);
  or or_4 (d, and_5_out, and_6_out, and_7_out, and_8_out, p3);
  or or_5 (e, and_9_out, and_10_out);
  or or_6 (f, and_11_out, and_12_out, and_13_out, p3);
  or or_7 (g, and_14_out, and_15_out, and_16_out, p3);
endmodule

module HA (
  input  in_1,
  input  in_2,
  output out_3,
  output out_4
);

  xor xor_1 (out_3, in_1, in_2);
  and and_1 (out_4, in_1, in_2);
endmodule

module CSA (
  input  x,
  input  y,
  input  clr,
  input  CLK,
  output sum
);

  wire d_ff_2_q, FDHA_2_out, FDHA_out, HA_out_3, HA_out_4, xor_1_out, xor_2_out;

  and FDHA (FDHA_out, HA_out_3, x);
  xor xor_1 (xor_1_out, x, HA_out_3);
  D_Flip_Flop d_ff_1 (.clk(CLK), .D(xor_1_out), .Q(sum), .reset(clr));  // open: Qn, preset, en
  HA HA (.in_1(y), .in_2(d_ff_2_q), .out_3(HA_out_3), .out_4(HA_out_4));
  xor xor_2 (xor_2_out, HA_out_4, FDHA_out);
  D_Flip_Flop d_ff_2 (.clk(CLK), .D(xor_2_out), .Q(d_ff_2_q), .reset(clr));  // open: Qn, preset, en
  and FDHA_2 (FDHA_2_out, FDHA_out, HA_out_4);

  // Notes on the sheet:
  //   sc
endmodule

module counter (
  input  clk,
  output out_2
);

  wire comparator_1_eq;
  wire [3:0] counter_1_q;

  Counter #(.width(4), .max('h8), .ongoal("stay")) counter_1 (
    .Q(counter_1_q), .clk(clk));  // open: load, D, count, carry, clr
  Comparator #(.width(4)) comparator_1 (.a(counter_1_q), .b(4'b1001), .eq(comparator_1_eq));  // open: gt, lt
  and and_1 (out_2, comparator_1_eq, clk);
endmodule

module mainnn (
  input  X7,
  input  X6,
  input  X5,
  input  X4,
  input  X3,
  input  X2,
  input  X1,
  input  X0,
  input  [7:0] in_9,
  input  in_10,
  input  in_11,
  input  crl,
  input  in_13,
  input  in_14
);

  wire and_1_out, and_2_out, and_3_out, and_4_out, and_5_out, and_6_out, and_7_out, and_8_out, clock_1_out,
       comparator_1_eq, csa_1_sum, csa_2_sum, csa_3_sum, csa_4_sum, csa_5_sum, csa_6_sum, csa_7_sum,
       multiplexer_1_out, not_1_out, shift_register_1_out, tcmp_1_out_4, to_bcd_1__0_2, to_bcd_1_out_17,
       to_bcd_1_out_18, to_bcd_1_out_19, to_bcd_1_out_20, to_bcd_1_out_21, to_bcd_1_out_22, to_bcd_1_out_23,
       to_bcd_1_out_24, to_bcd_1_out_25, to_bcd_1_out_26, to_bcd_1_out_27, to_bcd_1_out_28, to_bcd_1_out_29,
       to_bcd_1_out_30, to_bcd_1_out_31, to_bcd_1_out_32, to_bcd_1_out_33, to_bcd_1_out_34, undriven,
       unit_digit_1_a, unit_digit_1_b, unit_digit_1_c, unit_digit_1_d, unit_digit_1_e, unit_digit_1_f,
       unit_digit_1_g, unit_digit_2_g, unit_digit_3_a, unit_digit_3_b, unit_digit_3_c, unit_digit_3_d,
       unit_digit_3_e, unit_digit_3_f, unit_digit_3_g, unit_digit_4_a, unit_digit_4_b, unit_digit_4_c,
       unit_digit_4_d, unit_digit_4_e, unit_digit_4_f, unit_digit_4_g, unit_digit_5_a, unit_digit_5_b,
       unit_digit_5_c, unit_digit_5_d, unit_digit_5_e, unit_digit_5_f, unit_digit_5_g, unit_digit_6_a,
       unit_digit_6_b, unit_digit_6_c, unit_digit_6_d, unit_digit_6_e, unit_digit_6_f, unit_digit_6_g;
  wire [4:0] counter_1_q;
  wire [15:0] multiplexer_2_out, shift_register_2_q15, two_s_complement_16_bit_1_output;

  Shift_Register #(.length(16)) shift_register_1 (
    .clk(multiplexer_1_out), .out(shift_register_1_out), .load(in_10), .d0(in_9[7]), .d1(in_9[7]),
    .d2(in_9[7]), .d3(in_9[7]), .d4(in_9[7]), .d5(in_9[7]), .d6(in_9[7]), .d7(in_9[7]), .d8(in_9[7]),
    .d9(in_9[6]), .d10(in_9[5]), .d11(in_9[4]), .d12(in_9[3]), .d13(in_9[2]), .d14(in_9[1]), .d15(in_9[0]));  // open: shift, in, clr, q0, q1, q2, q3, q4, q5, q6, q7, q8, q9, q10, q11, q12, q13, q14, q15
  Multiplexer multiplexer_1 (.in0(in_10), .in1(clock_1_out), .out(multiplexer_1_out), .sel(in_11));  // open: en
  Clock clock_1 (.out(clock_1_out));
  Multiplexer #(.width(16)) multiplexer_2 (
    .in0(shift_register_2_q15), .in1(two_s_complement_16_bit_1_output), .out(multiplexer_2_out),
    .sel(shift_register_2_q15[15]), .en(undriven));
  Two_s_complement_16_bit two_s_complement_16_bit_1 (
    .\input (shift_register_2_q15), .\output (two_s_complement_16_bit_1_output));
  and and_1 (and_1_out, shift_register_1_out, X7);
  and and_2 (and_2_out, shift_register_1_out, X6);
  TCMP tcmp_1 (.A(and_1_out), .reset(crl), .out_4(tcmp_1_out_4), .clk(clock_1_out));
  and and_3 (and_3_out, shift_register_1_out, X5);
  CSA csa_1 (.x(and_2_out), .y(tcmp_1_out_4), .clr(crl), .CLK(clock_1_out), .sum(csa_1_sum));
  and and_4 (and_4_out, shift_register_1_out, X4);
  and and_5 (and_5_out, shift_register_1_out, X3);
  CSA csa_2 (.x(and_3_out), .y(csa_1_sum), .clr(crl), .CLK(clock_1_out), .sum(csa_2_sum));
  to_bcd to_bcd_1 (
    ._15(multiplexer_2_out[14]), .in_2(multiplexer_2_out[13]), .in_3(multiplexer_2_out[12]),
    .in_4(multiplexer_2_out[11]), .in_5(multiplexer_2_out[10]), .in_6(multiplexer_2_out[9]),
    .in_7(multiplexer_2_out[8]), .in_8(multiplexer_2_out[7]), .in_9(multiplexer_2_out[6]),
    .in_10(multiplexer_2_out[5]), .in_11(multiplexer_2_out[4]), .in_12(multiplexer_2_out[3]),
    .in_13(multiplexer_2_out[2]), .in_14(multiplexer_2_out[1]), ._0(multiplexer_2_out[0]),
    .out_17(to_bcd_1_out_17), .out_18(to_bcd_1_out_18), .out_19(to_bcd_1_out_19), .out_20(to_bcd_1_out_20),
    .out_21(to_bcd_1_out_21), .out_34(to_bcd_1_out_34), .out_22(to_bcd_1_out_22), .out_23(to_bcd_1_out_23),
    .out_24(to_bcd_1_out_24), .out_25(to_bcd_1_out_25), ._0_2(to_bcd_1__0_2), .out_26(to_bcd_1_out_26),
    .out_27(to_bcd_1_out_27), .out_28(to_bcd_1_out_28), .out_29(to_bcd_1_out_29), .out_30(to_bcd_1_out_30),
    .out_31(to_bcd_1_out_31), .out_32(to_bcd_1_out_32), .out_33(to_bcd_1_out_33));
  and and_6 (and_6_out, shift_register_1_out, X2);
  CSA csa_3 (.x(and_4_out), .y(csa_2_sum), .clr(crl), .CLK(clock_1_out), .sum(csa_3_sum));
  CSA csa_4 (.x(and_5_out), .y(csa_3_sum), .clr(crl), .CLK(clock_1_out), .sum(csa_4_sum));
  and and_7 (and_7_out, shift_register_1_out, X1);
  CSA csa_5 (.x(and_6_out), .y(csa_4_sum), .clr(crl), .CLK(clock_1_out), .sum(csa_5_sum));
  and and_8 (and_8_out, shift_register_1_out, X0);
  CSA csa_6 (.x(and_7_out), .y(csa_5_sum), .clr(crl), .CLK(clock_1_out), .sum(csa_6_sum));
  Shift_Register #(.length(16)) shift_register_2 (
    .shift(not_1_out), .in(csa_7_sum), .clk(clock_1_out), .clr(crl), .q0(shift_register_2_q15[15]),
    .q1(shift_register_2_q15[14]), .q2(shift_register_2_q15[13]), .q3(shift_register_2_q15[12]),
    .q4(shift_register_2_q15[11]), .q5(shift_register_2_q15[10]), .q6(shift_register_2_q15[9]),
    .q7(shift_register_2_q15[8]), .q8(shift_register_2_q15[7]), .q9(shift_register_2_q15[6]),
    .q10(shift_register_2_q15[5]), .q11(shift_register_2_q15[4]), .q12(shift_register_2_q15[3]),
    .q13(shift_register_2_q15[2]), .q14(shift_register_2_q15[1]), .q15(shift_register_2_q15[0]));  // open: out, load, d0, d1, d2, d3, d4, d5, d6, d7, d8, d9, d10, d11, d12, d13, d14, d15
  CSA csa_7 (.x(and_8_out), .y(csa_6_sum), .clr(crl), .CLK(clock_1_out), .sum(csa_7_sum));
  unit_digit unit_digit_1 (
    .p3(to_bcd_1_out_31), .p2(to_bcd_1_out_32), .p1(to_bcd_1_out_33), .p0(to_bcd_1__0_2), .a(unit_digit_1_a),
    .b(unit_digit_1_b), .c(unit_digit_1_c), .d(unit_digit_1_d), .e(unit_digit_1_e), .f(unit_digit_1_f),
    .g(unit_digit_1_g));
  Counter #(.width(5), .max('h11), .ongoal("stay")) counter_1 (
    .Q(counter_1_q), .clk(clock_1_out));  // open: load, D, count, carry, clr
  unit_digit unit_digit_2 (
    .p3(shift_register_2_q15[15]), .p2(in_13), .p1(in_13), .p0(in_13), .g(unit_digit_2_g));  // open: a, b, c, d, e, f
  _7_Segment_Display u_7_segment_display_1 (
    .g(unit_digit_1_g), .f(unit_digit_1_f), .a(unit_digit_1_a), .b(unit_digit_1_b), .e(unit_digit_1_e),
    .d(unit_digit_1_d), .c(unit_digit_1_c));  // open: dp
  unit_digit unit_digit_3 (
    .p3(to_bcd_1_out_23), .p2(to_bcd_1_out_24), .p1(to_bcd_1_out_25), .p0(to_bcd_1_out_26),
    .a(unit_digit_3_a), .b(unit_digit_3_b), .c(unit_digit_3_c), .d(unit_digit_3_d), .e(unit_digit_3_e),
    .f(unit_digit_3_f), .g(unit_digit_3_g));
  not not_1 (not_1_out, comparator_1_eq);
  Comparator #(.width(5), .mode("unsigned")) comparator_1 (
    .a(counter_1_q), .b(5'b10001), .eq(comparator_1_eq));  // open: gt, lt
  _7_Segment_Display u_7_segment_display_2 (.g(unit_digit_2_g));  // open: f, a, b, e, d, c, dp
  unit_digit unit_digit_4 (
    .p3(to_bcd_1_out_27), .p2(to_bcd_1_out_28), .p1(to_bcd_1_out_29), .p0(to_bcd_1_out_30),
    .a(unit_digit_4_a), .b(unit_digit_4_b), .c(unit_digit_4_c), .d(unit_digit_4_d), .e(unit_digit_4_e),
    .f(unit_digit_4_f), .g(unit_digit_4_g));
  unit_digit unit_digit_5 (
    .p3(to_bcd_1_out_20), .p2(to_bcd_1_out_21), .p1(to_bcd_1_out_34), .p0(to_bcd_1_out_22),
    .a(unit_digit_5_a), .b(unit_digit_5_b), .c(unit_digit_5_c), .d(unit_digit_5_d), .e(unit_digit_5_e),
    .f(unit_digit_5_f), .g(unit_digit_5_g));
  unit_digit unit_digit_6 (
    .p3(in_14), .p2(to_bcd_1_out_17), .p1(to_bcd_1_out_18), .p0(to_bcd_1_out_19), .a(unit_digit_6_a),
    .b(unit_digit_6_b), .c(unit_digit_6_c), .d(unit_digit_6_d), .e(unit_digit_6_e), .f(unit_digit_6_f),
    .g(unit_digit_6_g));
  _7_Segment_Display u_7_segment_display_3 (
    .g(unit_digit_3_g), .f(unit_digit_3_f), .a(unit_digit_3_a), .b(unit_digit_3_b), .e(unit_digit_3_e),
    .d(unit_digit_3_d), .c(unit_digit_3_c));  // open: dp
  _7_Segment_Display u_7_segment_display_4 (
    .g(unit_digit_6_g), .f(unit_digit_6_f), .a(unit_digit_6_a), .b(unit_digit_6_b), .e(unit_digit_6_e),
    .d(unit_digit_6_d), .c(unit_digit_6_c));  // open: dp
  _7_Segment_Display u_7_segment_display_5 (
    .g(unit_digit_4_g), .f(unit_digit_4_f), .a(unit_digit_4_a), .b(unit_digit_4_b), .e(unit_digit_4_e),
    .d(unit_digit_4_d), .c(unit_digit_4_c));  // open: dp
  _7_Segment_Display u_7_segment_display_6 (
    .g(unit_digit_5_g), .f(unit_digit_5_f), .a(unit_digit_5_a), .b(unit_digit_5_b), .e(unit_digit_5_e),
    .d(unit_digit_5_d), .c(unit_digit_5_c));  // open: dp

  // Notes on the sheet:
  //   units
  //   hundreds
  //   thousands
  //   ten thousands 
  //   sign
  //   tens
endmodule

module ADD_3 (
  input  A3,
  input  A2,
  input  A1,
  input  A0,
  output S3,
  output S2,
  output S1,
  output S0
);

  wire and_1_out, and_2_out, and_3_out, and_4_out, and_5_out, and_6_out, and_7_out, and_8_out, and_9_out,
       and_10_out, not_1_out, not_2_out, not_3_out, not_4_out, not_5_out, not_6_out, not_7_out, not_8_out;

  and and_1 (and_1_out, A2, A0);
  and and_2 (and_2_out, A2, A1);
  and and_3 (and_3_out, A2, not_1_out, not_2_out);
  not not_1 (not_1_out, A1);
  not not_2 (not_2_out, A0);
  and and_4 (and_4_out, A3, A0);
  not not_3 (not_3_out, A2);
  and and_5 (and_5_out, not_3_out, A1);
  and and_6 (and_6_out, A1, A0);
  and and_7 (and_7_out, A3, not_4_out);
  not not_4 (not_4_out, A0);
  not not_5 (not_5_out, A3);
  not not_6 (not_6_out, A2);
  and and_8 (and_8_out, not_5_out, not_6_out, A0);
  and and_9 (and_9_out, A2, A1, not_7_out);
  not not_7 (not_7_out, A0);
  and and_10 (and_10_out, A3, not_8_out);
  not not_8 (not_8_out, A0);
  or or_1 (S3, and_1_out, and_2_out, A3);
  or or_2 (S2, and_3_out, and_4_out);
  or or_3 (S1, and_5_out, and_6_out, and_7_out);
  or or_4 (S0, and_8_out, and_9_out, and_10_out);
endmodule

module to_bcd (
  input  _15,
  input  in_2,
  input  in_3,
  input  in_4,
  input  in_5,
  input  in_6,
  input  in_7,
  input  in_8,
  input  in_9,
  input  in_10,
  input  in_11,
  input  in_12,
  input  in_13,
  input  in_14,
  input  _0,
  output _0_2,
  output out_17,
  output out_18,
  output out_19,
  output out_20,
  output out_21,
  output out_22,
  output out_23,
  output out_24,
  output out_25,
  output out_26,
  output out_27,
  output out_28,
  output out_29,
  output out_30,
  output out_31,
  output out_32,
  output out_33,
  output out_34
);

  wire add_3_1_s0, add_3_1_s1, add_3_1_s2, add_3_1_s3, add_3_2_s0, add_3_2_s1, add_3_2_s2, add_3_2_s3,
       add_3_3_s0, add_3_3_s1, add_3_3_s2, add_3_3_s3, add_3_4_s0, add_3_4_s1, add_3_4_s2, add_3_4_s3,
       add_3_5_s0, add_3_5_s1, add_3_5_s2, add_3_5_s3, add_3_6_s0, add_3_6_s1, add_3_6_s2, add_3_6_s3,
       add_3_7_s0, add_3_7_s1, add_3_7_s2, add_3_7_s3, add_3_8_s0, add_3_8_s1, add_3_8_s2, add_3_8_s3,
       add_3_9_s0, add_3_9_s1, add_3_9_s2, add_3_9_s3, add_3_10_s0, add_3_10_s1, add_3_10_s2, add_3_10_s3,
       add_3_11_s0, add_3_11_s1, add_3_11_s2, add_3_11_s3, add_3_12_s0, add_3_12_s1, add_3_12_s2,
       add_3_12_s3, add_3_13_s0, add_3_13_s1, add_3_13_s2, add_3_13_s3, add_3_14_s0, add_3_14_s1,
       add_3_14_s2, add_3_14_s3, add_3_15_s0, add_3_15_s1, add_3_15_s2, add_3_16_s0, add_3_16_s1,
       add_3_16_s2, add_3_16_s3, add_3_17_s0, add_3_17_s1, add_3_17_s2, add_3_17_s3, add_3_18_s0,
       add_3_18_s1, add_3_18_s2, add_3_20_s0, add_3_20_s1, add_3_20_s2, add_3_20_s3, add_3_21_s0,
       add_3_21_s1, add_3_21_s2, add_3_21_s3, add_3_22_s0, add_3_22_s1, add_3_22_s2, add_3_22_s3,
       add_3_23_s0, add_3_23_s1, add_3_23_s2, add_3_23_s3, add_3_25_s0, add_3_25_s1, add_3_25_s2,
       add_3_25_s3, add_3_26_s0, add_3_26_s1, add_3_26_s2, add_3_26_s3, add_3_27_s0, add_3_27_s1,
       add_3_27_s2, add_3_27_s3, add_3_29_s0, add_3_29_s1, add_3_29_s2, add_3_29_s3;

  ADD_3 add_3_1 (
    .A3(1'b0), .A2(_15), .A1(in_2), .A0(in_3), .S3(add_3_1_s3), .S2(add_3_1_s2), .S1(add_3_1_s1),
    .S0(add_3_1_s0));
  ADD_3 add_3_2 (
    .A3(add_3_1_s2), .A2(add_3_1_s1), .A1(add_3_1_s0), .A0(in_4), .S3(add_3_2_s3), .S2(add_3_2_s2),
    .S1(add_3_2_s1), .S0(add_3_2_s0));
  ADD_3 add_3_3 (
    .A3(1'b0), .A2(add_3_1_s3), .A1(add_3_2_s3), .A0(add_3_4_s3), .S3(add_3_3_s3), .S2(add_3_3_s2),
    .S1(add_3_3_s1), .S0(add_3_3_s0));
  ADD_3 add_3_4 (
    .A3(add_3_2_s2), .A2(add_3_2_s1), .A1(add_3_2_s0), .A0(in_5), .S3(add_3_4_s3), .S2(add_3_4_s2),
    .S1(add_3_4_s1), .S0(add_3_4_s0));
  ADD_3 add_3_5 (
    .A3(add_3_3_s2), .A2(add_3_3_s1), .A1(add_3_3_s0), .A0(add_3_6_s3), .S3(add_3_5_s3), .S2(add_3_5_s2),
    .S1(add_3_5_s1), .S0(add_3_5_s0));
  ADD_3 add_3_6 (
    .A3(add_3_4_s2), .A2(add_3_4_s1), .A1(add_3_4_s0), .A0(in_6), .S3(add_3_6_s3), .S2(add_3_6_s2),
    .S1(add_3_6_s1), .S0(add_3_6_s0));
  ADD_3 add_3_7 (
    .A3(add_3_6_s2), .A2(add_3_6_s1), .A1(add_3_6_s0), .A0(in_7), .S3(add_3_7_s3), .S2(add_3_7_s2),
    .S1(add_3_7_s1), .S0(add_3_7_s0));
  ADD_3 add_3_8 (
    .A3(add_3_5_s2), .A2(add_3_5_s1), .A1(add_3_5_s0), .A0(add_3_7_s3), .S3(add_3_8_s3), .S2(add_3_8_s2),
    .S1(add_3_8_s1), .S0(add_3_8_s0));
  ADD_3 add_3_9 (
    .A3(1'b0), .A2(add_3_3_s3), .A1(add_3_5_s3), .A0(add_3_8_s3), .S3(add_3_9_s3), .S2(add_3_9_s2),
    .S1(add_3_9_s1), .S0(add_3_9_s0));
  ADD_3 add_3_10 (
    .A3(add_3_7_s2), .A2(add_3_7_s1), .A1(add_3_7_s0), .A0(in_8), .S3(add_3_10_s3), .S2(add_3_10_s2),
    .S1(add_3_10_s1), .S0(add_3_10_s0));
  ADD_3 add_3_11 (
    .A3(add_3_8_s2), .A2(add_3_8_s1), .A1(add_3_8_s0), .A0(add_3_10_s3), .S3(add_3_11_s3), .S2(add_3_11_s2),
    .S1(add_3_11_s1), .S0(add_3_11_s0));
  ADD_3 add_3_12 (
    .A3(add_3_9_s2), .A2(add_3_9_s1), .A1(add_3_9_s0), .A0(add_3_11_s3), .S3(add_3_12_s3), .S2(add_3_12_s2),
    .S1(add_3_12_s1), .S0(add_3_12_s0));
  ADD_3 add_3_13 (
    .A3(add_3_12_s2), .A2(add_3_12_s1), .A1(add_3_12_s0), .A0(add_3_14_s3), .S3(add_3_13_s3),
    .S2(add_3_13_s2), .S1(add_3_13_s1), .S0(add_3_13_s0));
  ADD_3 add_3_14 (
    .A3(add_3_11_s2), .A2(add_3_11_s1), .A1(add_3_11_s0), .A0(add_3_16_s3), .S3(add_3_14_s3),
    .S2(add_3_14_s2), .S1(add_3_14_s1), .S0(add_3_14_s0));
  ADD_3 add_3_15 (
    .A3(1'b0), .A2(add_3_9_s3), .A1(add_3_12_s3), .A0(add_3_13_s3), .S3(out_17), .S2(add_3_15_s2),
    .S1(add_3_15_s1), .S0(add_3_15_s0));
  ADD_3 add_3_16 (
    .A3(add_3_10_s2), .A2(add_3_10_s1), .A1(add_3_10_s0), .A0(in_9), .S3(add_3_16_s3), .S2(add_3_16_s2),
    .S1(add_3_16_s1), .S0(add_3_16_s0));
  ADD_3 add_3_17 (
    .A3(add_3_14_s2), .A2(add_3_14_s1), .A1(add_3_14_s0), .A0(add_3_20_s3), .S3(add_3_17_s3),
    .S2(add_3_17_s2), .S1(add_3_17_s1), .S0(add_3_17_s0));
  ADD_3 add_3_18 (
    .A3(add_3_15_s2), .A2(add_3_15_s1), .A1(add_3_15_s0), .A0(add_3_21_s3), .S3(out_18), .S2(add_3_18_s2),
    .S1(add_3_18_s1), .S0(add_3_18_s0));
  ADD_3 add_3_19 (
    .A3(add_3_18_s2), .A2(add_3_18_s1), .A1(add_3_18_s0), .A0(add_3_23_s3), .S3(out_19), .S2(out_20),
    .S1(out_21), .S0(out_34));
  ADD_3 add_3_20 (
    .A3(add_3_16_s2), .A2(add_3_16_s1), .A1(add_3_16_s0), .A0(in_10), .S3(add_3_20_s3), .S2(add_3_20_s2),
    .S1(add_3_20_s1), .S0(add_3_20_s0));
  ADD_3 add_3_21 (
    .A3(add_3_13_s2), .A2(add_3_13_s1), .A1(add_3_13_s0), .A0(add_3_17_s3), .S3(add_3_21_s3),
    .S2(add_3_21_s2), .S1(add_3_21_s1), .S0(add_3_21_s0));
  ADD_3 add_3_22 (
    .A3(add_3_20_s2), .A2(add_3_20_s1), .A1(add_3_20_s0), .A0(in_11), .S3(add_3_22_s3), .S2(add_3_22_s2),
    .S1(add_3_22_s1), .S0(add_3_22_s0));
  ADD_3 add_3_23 (
    .A3(add_3_21_s2), .A2(add_3_21_s1), .A1(add_3_21_s0), .A0(add_3_25_s3), .S3(add_3_23_s3),
    .S2(add_3_23_s2), .S1(add_3_23_s1), .S0(add_3_23_s0));
  ADD_3 add_3_24 (
    .A3(add_3_23_s2), .A2(add_3_23_s1), .A1(add_3_23_s0), .A0(add_3_26_s3), .S3(out_22), .S2(out_23),
    .S1(out_24), .S0(out_25));
  ADD_3 add_3_25 (
    .A3(add_3_17_s2), .A2(add_3_17_s1), .A1(add_3_17_s0), .A0(add_3_22_s3), .S3(add_3_25_s3),
    .S2(add_3_25_s2), .S1(add_3_25_s1), .S0(add_3_25_s0));
  ADD_3 add_3_26 (
    .A3(add_3_25_s2), .A2(add_3_25_s1), .A1(add_3_25_s0), .A0(add_3_27_s3), .S3(add_3_26_s3),
    .S2(add_3_26_s2), .S1(add_3_26_s1), .S0(add_3_26_s0));
  ADD_3 add_3_27 (
    .A3(add_3_22_s2), .A2(add_3_22_s1), .A1(add_3_22_s0), .A0(in_12), .S3(add_3_27_s3), .S2(add_3_27_s2),
    .S1(add_3_27_s1), .S0(add_3_27_s0));
  ADD_3 add_3_28 (
    .A3(add_3_26_s2), .A2(add_3_26_s1), .A1(add_3_26_s0), .A0(add_3_29_s3), .S3(out_26), .S2(out_27),
    .S1(out_28), .S0(out_29));
  ADD_3 add_3_29 (
    .A3(add_3_27_s2), .A2(add_3_27_s1), .A1(add_3_27_s0), .A0(in_13), .S3(add_3_29_s3), .S2(add_3_29_s2),
    .S1(add_3_29_s1), .S0(add_3_29_s0));
  ADD_3 add_3_30 (
    .A3(add_3_29_s2), .A2(add_3_29_s1), .A1(add_3_29_s0), .A0(in_14), .S3(out_30), .S2(out_31), .S1(out_32),
    .S0(out_33));

  assign _0_2 = _0;
endmodule

module Two_s_complement_16_bit (
  input  [15:0] \input ,
  output [15:0] \output 
);

  wire [15:0] not_1_out;

  assign not_1_out = ~\input ;  // NOT_Gate not_1, 16 bits wide
  Adder #(.width(16)) adder_1 (.a(not_1_out), .b(16'h1), .out(\output ));  // open: cin, cout
endmodule
